// Logisim project subtractor.circ as structural Verilog: 1 circuit, main circuit main
module main (
  input  a3,
  input  a2,
  input  a1,
  input  a0,
  input  b2,
  input  b1,
  input  b0,
  input  in_8,
  input  Cin,
  output Cout,
  output S3,
  output S2,
  output S1,
  output S0
);

  wire and_1_out, and_2_out, and_3_out, and_4_out, and_5_out, and_6_out, and_7_out, and_8_out, not_1_out,
       not_2_out, not_3_out, not_4_out, or_1_out, or_2_out, or_3_out, xor_1_out, xor_3_out, xor_5_out,
       xor_7_out;

  not not_1 (not_1_out, a0);
  xor xor_1 (xor_1_out, not_1_out, in_8);
  and and_1 (and_1_out, in_8, not_1_out);
  xor xor_2 (S0, xor_1_out, Cin);
  and and_2 (and_2_out, Cin, xor_1_out);
  or or_1 (or_1_out, and_2_out, and_1_out);
  not not_2 (not_2_out, a1);
  xor xor_3 (xor_3_out, not_2_out, b0);
  and and_3 (and_3_out, b0, not_2_out);
  and and_4 (and_4_out, or_1_out, xor_3_out);
  xor xor_4 (S1, xor_3_out, or_1_out);
  or or_2 (or_2_out, and_4_out, and_3_out);
  not not_3 (not_3_out, a2);
  xor xor_5 (xor_5_out, not_3_out, b1);
  and and_5 (and_5_out, b1, not_3_out);
  and and_6 (and_6_out, or_2_out, xor_5_out);
  xor xor_6 (S2, xor_5_out, or_2_out);
  or or_3 (or_3_out, and_6_out, and_5_out);
  not not_4 (not_4_out, a3);
  xor xor_7 (xor_7_out, not_4_out, b2);
  and and_7 (and_7_out, b2, not_4_out);
  xor xor_8 (S3, xor_7_out, or_3_out);
  and and_8 (and_8_out, or_3_out, xor_7_out);
  or or_4 (Cout, and_8_out, and_7_out);

  // Notes on the sheet:
  //   4 bit subtractor circuit
  //   b3
  //        0010-1000=0110
  //                              1111-1000=0111
endmodule
